// Logisim project b-machine.circ as structural Verilog
module main (
  input  Reset
);

  wire BSEL, RA2SEL, WERF, WR;
  wire [1:0] PCSEL, WDSEL;
  wire [3:0] ALUFN;
  wire [4:0] instruction_memory_1_data_3, multiplexer_2_out;
  wire [5:0] instruction_memory_1_data_4;
  wire [15:0] instruction_memory_1_data;
  wire [20:16] instruction_memory_1_data_2;
  wire [31:0] alu_1_out, data_memory_1_rd, JT, multiplexer_1_out, multiplexer_3_out, multiplexer_4_out,
       n4_1_out, part_1_out, pc_1_out, register_file_1_rd2, sext_1_out;

  Clock Clock ();  // open: out
  Multiplexer #(.select(2), .width(32), .enable("false")) multiplexer_1 (
    .in0(n4_1_out), .in1(part_1_out), .in2(JT), .out(multiplexer_1_out), .sel(PCSEL));  // open: in3
  PC pc_1 (.In(multiplexer_1_out), .Reset(Reset), .Out(pc_1_out));
  _4 u_4_1 (.In(pc_1_out), .Out(n4_1_out));
  Control_logic control_logic_1 ();
  circuit part_1 (.In_1(sext_1_out), .In_2(n4_1_out), .Out(part_1_out));
  Instruction_memory instruction_memory_1 (
    .Address(pc_1_out),
    .Data({instruction_memory_1_data_4, instruction_memory_1_data_3, instruction_memory_1_data_2, instruction_memory_1_data}));
  SEXT sext_1 (.In(instruction_memory_1_data), .Out(sext_1_out));
  Register_file register_file_1 (
    .WA(instruction_memory_1_data_3), .WE(WERF), .WD(multiplexer_4_out), .RA1(instruction_memory_1_data_2),
    .RA2(multiplexer_2_out), .RD1(JT), .RD2(register_file_1_rd2));
  Multiplexer #(.width(5), .enable("false")) multiplexer_2 (
    .in0(instruction_memory_1_data[15:11]), .in1(instruction_memory_1_data_3), .out(multiplexer_2_out),
    .sel(RA2SEL));
  Multiplexer #(.width(32), .enable("false")) multiplexer_3 (
    .in0(sext_1_out), .in1(register_file_1_rd2), .out(multiplexer_3_out), .sel(BSEL));
  ALU alu_1 (.A(JT), .B(multiplexer_3_out), .OUT(alu_1_out), .RA1(ALUFN));
  Multiplexer #(.select(2), .width(32), .enable("false")) multiplexer_4 (
    .in0(n4_1_out), .in1(alu_1_out), .in2(data_memory_1_rd), .out(multiplexer_4_out), .sel(WDSEL));  // open: in3
  Data_memory data_memory_1 (.Address(alu_1_out), .WR(WR), .RD(data_memory_1_rd), .WD(register_file_1_rd2));
endmodule

module ALU (
  input  [31:0] A,
  input  [3:0] RA1,
  input  [31:0] B,
  output [31:0] OUT
);

  wire comparator_1_eq, comparator_1_gt, comparator_1_lt;
  wire [31:0] adder_1_out, and_1_out, bit_extender_1_out, bit_extender_2_out, bit_extender_3_out,
       divider_1_out, multiplier_1_out, or_1_out, shifter_1_out, shifter_2_out, shifter_3_out,
       subtractor_1_out, xor_1_out;

  Adder #(.width(32)) adder_1 (.a(A), .b(B), .out(adder_1_out));  // open: cin, cout
  Subtractor #(.width(32)) subtractor_1 (.a(B), .b(A), .out(subtractor_1_out));  // open: bin, bout
  Multiplier #(.width(32)) multiplier_1 (.a(B), .b(A), .out(multiplier_1_out));  // open: cin, cout
  Divider #(.width(32)) divider_1 (.a(B), .b(A), .out(divider_1_out));  // open: upper, rem
  assign and_1_out = A & B;  // AND_Gate and_1, 32 bits wide
  assign or_1_out = A | B;  // OR_Gate or_1, 32 bits wide
  assign xor_1_out = A ^ B;  // XOR_Gate xor_1, 32 bits wide
  Comparator #(.width(32)) comparator_1 (
    .a(A), .b(B), .gt(comparator_1_gt), .eq(comparator_1_eq), .lt(comparator_1_lt));
  Shifter #(.width(32), .shift("ar")) shifter_1 (.in(A), .\dist (B[4:0]), .out(shifter_1_out));
  Shifter #(.width(32), .shift("lr")) shifter_2 (.in(A), .\dist (B[4:0]), .out(shifter_2_out));
  Shifter #(.width(32)) shifter_3 (.in(A), .\dist (B[4:0]), .out(shifter_3_out));
  assign bit_extender_1_out = {{31{comparator_1_gt}}, comparator_1_gt};  // Bit_Extender bit_extender_1
  assign bit_extender_2_out = {{31{comparator_1_eq}}, comparator_1_eq};  // Bit_Extender bit_extender_2
  assign bit_extender_3_out = {{31{comparator_1_lt}}, comparator_1_lt};  // Bit_Extender bit_extender_3
  Multiplexer #(.select(4), .width(32), .enable("false")) multiplexer_1 (
    .in1(adder_1_out), .in2(subtractor_1_out), .in3(multiplier_1_out), .in4(divider_1_out), .in5(and_1_out),
    .in6(or_1_out), .in7(xor_1_out), .in8(bit_extender_1_out), .in9(bit_extender_2_out),
    .in10(bit_extender_3_out), .in11(shifter_3_out), .in12(shifter_2_out), .in13(shifter_1_out), .out(OUT),
    .sel(RA1));  // open: in0, in14, in15
endmodule

module PC (
  input  [31:0] In,
  input  Reset,
  output [31:0] Out
);

  wire Clock_out;

  Clock Clock (.out(Clock_out));
  Register #(.width(32)) PC (.D(In), .Q(Out), .clk(Clock_out), .clr(Reset));  // open: en
endmodule

module _4 (
  input  [31:0] In,
  output [31:0] Out
);

  Adder #(.width(32)) adder_1 (.a(In), .b(32'h4), .out(Out));  // open: cin, cout
endmodule

module Instruction_memory (
  input  [31:0] Address,
  output [31:0] Data
);

  ROM #(.addrWidth(10), .dataWidth(32)) rom_1 (.addr(Address[9:0]), .data(Data));  // open: sel
endmodule

module Register_file (
  input  WE,
  input  [4:0] WA,
  input  [31:0] WD,
  input  [4:0] RA2,
  input  [4:0] RA1,
  output [31:0] RD1,
  output [31:0] RD2
);

  wire clock_1_out, demultiplexer_1_out0, demultiplexer_1_out1, demultiplexer_1_out2, demultiplexer_1_out3,
       demultiplexer_1_out28, demultiplexer_1_out29, demultiplexer_1_out30;
  wire [31:0] r0_q, r1_q, r2_q, r3_q, r28_q, r29_q, r30_q;

  Register #(.width(32)) r0 (.D(WD), .en(demultiplexer_1_out0), .Q(r0_q), .clk(clock_1_out));  // open: clr
  Clock clock_1 (.out(clock_1_out));
  Register #(.width(32)) r1 (.D(WD), .en(demultiplexer_1_out1), .Q(r1_q), .clk(clock_1_out));  // open: clr
  Multiplexer #(.select(5), .width(32), .enable("false")) multiplexer_1 (
    .in0(r0_q), .in1(r1_q), .in2(r2_q), .in3(r3_q), .in28(r28_q), .in29(r29_q), .in30(r30_q),
    .in31({32{1'b0}}), .out(RD1), .sel(RA1));  // open: in4, in5, in6, in7, in8, in9, in10, in11, in12, in13, in14, in15, in16, in17, in18, in19, in20, in21, in22, in23, in24, in25, in26, in27
  Register #(.width(32)) r2 (.D(WD), .en(demultiplexer_1_out2), .Q(r2_q), .clk(clock_1_out));  // open: clr
  Register #(.width(32)) r3 (.D(WD), .en(demultiplexer_1_out3), .Q(r3_q), .clk(clock_1_out));  // open: clr
  Demultiplexer #(.select(5), .enable("false")) demultiplexer_1 (
    .out0(demultiplexer_1_out0), .out1(demultiplexer_1_out1), .out2(demultiplexer_1_out2),
    .out3(demultiplexer_1_out3), .out28(demultiplexer_1_out28), .out29(demultiplexer_1_out29),
    .out30(demultiplexer_1_out30), .in(WE), .sel(WA));  // open: out4, out5, out6, out7, out8, out9, out10, out11, out12, out13, out14, out15, out16, out17, out18, out19, out20, out21, out22, out23, out24, out25, out26, out27, out31
  Register #(.width(32)) r28 (.D(WD), .en(demultiplexer_1_out28), .Q(r28_q), .clk(clock_1_out));  // open: clr
  Register #(.width(32)) r29 (.D(WD), .en(demultiplexer_1_out29), .Q(r29_q), .clk(clock_1_out));  // open: clr
  Register #(.width(32)) r30 (.D(WD), .en(demultiplexer_1_out30), .Q(r30_q), .clk(clock_1_out));  // open: clr
  Multiplexer #(.select(5), .width(32), .enable("false")) multiplexer_2 (
    .in0(r0_q), .in1(r1_q), .in2(r2_q), .in3(r3_q), .in28(r28_q), .in29(r29_q), .in30(r30_q),
    .in31({32{1'b0}}), .out(RD2), .sel(RA2));  // open: in4, in5, in6, in7, in8, in9, in10, in11, in12, in13, in14, in15, in16, in17, in18, in19, in20, in21, in22, in23, in24, in25, in26, in27
endmodule

module Data_memory (
  input  [31:0] Address,
  input  [31:0] WD,
  input  WR,
  output [31:0] RD
);

  wire clock_1_out, not_1_out;

  not not_1 (not_1_out, WR);
  Clock clock_1 (.out(clock_1_out));
  RAM #(.addrWidth(10), .dataWidth(32), .bus("separate")) ram_1 (
    .addr(Address[9:0]), .din(WD), .data(RD), .str(WR), .clk(clock_1_out), .ld(not_1_out));  // open: sel, clr
endmodule

module SEXT (
  input  [15:0] In,
  output [31:0] Out
);

  assign Out = {{16{In[15]}}, In};  // Bit_Extender bit_extender_1
endmodule

module circuit (
  input  [31:0] In_1,
  input  [31:0] In_2,
  output [31:0] Out
);

  Adder #(.width(32)) adder_1 (.a(In_1), .b(In_2), .out(Out));  // open: cin, cout
endmodule
